# Fritzing sketch connexionat emces_apagat amb un boto (saved by Fritzing 0.9.5d)
breadboards: 1

parts:
  Raspberry_Pi_1 = Raspberry Pi 3 [part_number=RPI-3-V1.2]
  S1 = Momentary Switch [package=ksa_sealed_tac_switch]
  D1 = Diode [package=diode-1n4148]
  D2 = Diode [package=diode-1n4148]

nets:
  N1: Raspberry_Pi_1.GPIO3, D2.C
  N2: Raspberry_Pi_1.GPIO17, D1.C
  N3: Raspberry_Pi_1.GND, S1.1

notes:
  GPIO3
  encendido
  GPIO17
  apagado
